# Fritzing sketch Sketch FIX (saved by Fritzing 0.9.3b)
breadboards: 1

parts:
  LM7805_IC4 = Voltage Regulator [package=to-220-alt]
  U1 = ESP8266 NodeMCU LoLin module
  VCC1 = Battery
  hc-sr1 = hc-sr04

nets:
  GND: LM7805_IC4.GND, U1.GND, VCC1.-, hc-sr1.GND
  N1: LM7805_IC4.IN, U1.Vin, VCC1.+
  N2: LM7805_IC4.OUT, hc-sr1.VCC
  N3: U1.D1, hc-sr1.Trig
  N4: U1.D2, hc-sr1.Echo

custom parts:
  ESP8266 NodeMCU LoLin module: ESP8266 based NodeMCU
