# Fritzing sketch Sketch di Kotak Sampah (saved by Fritzing 0.9.3b)
breadboards: 1

parts:
  U1 = ESP8266 NodeMCU LoLin module
  hc-sr1 = hc-sr04

nets:
  3V3: U1.3V3, hc-sr1.VCC
  GND: U1.GND, hc-sr1.GND
  N1: U1.D7, hc-sr1.Echo
  N2: U1.D8, hc-sr1.Trig

custom parts:
  ESP8266 NodeMCU LoLin module: ESP8266 based NodeMCU
